# Fritzing sketch wiring (saved by Fritzing 0.9.2b)

parts:
  Part1 = Arduino Ethernet Shield (Rev3)
  R1 = Resistor [tolerance=±5% resistance=10k package=THT]
  DHT11 = DHT11 Humitidy and Temperature Sensor
  S1 = SWITCH-MOMENTARY-2 [package=tactile-switch-1101ne]
  S2 = SWITCH-MOMENTARY-2 [package=tactile-switch-1101ne]
  R2 = Resistor [tolerance=±5% resistance=10k package=THT]
  Q1 = Basic FET N-Channel [package="TO220 [THT]"]
  D1 = Diode [package=diode-1n4001]
  J1 = Screw terminal - 2 pins [package=THT]
  J2 = Screw terminal - 2 pins [package=THT]

nets:
  N1: Part1.GND, R2.Pin_1, J1.pin2, J2.pin2
  N2: Part1.D2, R1.Pin_0, DHT11.DATA
  N3: Part1.PWM_D3, S1.1, S2.1, R2.Pin_0, Q1.gate
  5V: Part1.5V, R1.Pin_1, DHT11.VDD, S1.2, S2.2
  N4: Part1.VIN, Q1.drain, D1.C
  N5: Q1.source, J2.pin1
  N6: D1.A, J1.pin1

notes:
  <-- + 12V input DC
  <-- GND input
  <-- + 12V LEDs output
  <-- GND output
  + 12V input DC -->
  GND input -->
  G
  D
  S

custom parts:
  DHT11 Humitidy and Temperature Sensor: DHT11 Humidity and Temperature Sensor
